# Fritzing sketch カップラーメンタイマー (saved by Fritzing 0.9.3b)
breadboards: 1

parts:
  Arduino_UNO = Arduino Uno (Rev3)
  7_Segment_4_Digit_Display1 = 7-SEGMENT-4DIGIT common anode [part_number="5461BS - 5462BS" package=7-segment-4digit-anode]
  R1 = Resistor [tolerance=±5% resistance=220 package=THT]
  R2 = Resistor [tolerance=±5% resistance=220 package=THT]
  R3 = Resistor [tolerance=±5% resistance=220 package=THT]
  R4 = Resistor [tolerance=±5% resistance=220 package=THT]
  R5 = Resistor [tolerance=±5% resistance=220 package=THT]
  R6 = Resistor [tolerance=±5% resistance=220 package=THT]
  R7 = Resistor [tolerance=±5% resistance=220 package=THT]
  R8 = Resistor [tolerance=±5% resistance=220 package=THT]
  スイッチ = Pushbutton [package="[THT]"]
  R9 = Resistor [tolerance=±5% resistance=10k package=THT]
  アクティブブザー = KY-012 Active Buzzer Module [package="Breakout board"]

nets:
  N1: Arduino_UNO.D8, R6.Pin_1
  N2: Arduino_UNO.D9_PWM, 7_Segment_4_Digit_Display1.pin_6
  N3: Arduino_UNO.D10_PWM/SS, 7_Segment_4_Digit_Display1.pin_8
  N4: Arduino_UNO.D11_PWM/MOSI, 7_Segment_4_Digit_Display1.pin_9
  N5: Arduino_UNO.D12/MISO, 7_Segment_4_Digit_Display1.pin_12
  5V: Arduino_UNO.D13/SCK, Arduino_UNO.5V, スイッチ.Pin_1, スイッチ.Pin_2
  N6: Arduino_UNO.D0/RX, アクティブブザー.S
  N7: Arduino_UNO.D1/TX, R1.Pin_0
  N8: Arduino_UNO.D2, R3.Pin_0
  N9: Arduino_UNO.D3_PWM, R7.Pin_1
  N10: Arduino_UNO.D4, R5.Pin_1
  N11: Arduino_UNO.D5_PWM, R4.Pin_1
  N12: Arduino_UNO.D6_PWM, R2.Pin_0
  N13: Arduino_UNO.D7, R8.Pin_1
  GND: Arduino_UNO.GND, R9.Pin_1, アクティブブザー.-
  N14: 7_Segment_4_Digit_Display1.pin_1, R4.Pin_0
  N15: 7_Segment_4_Digit_Display1.pin_2, R5.Pin_0
  N16: 7_Segment_4_Digit_Display1.pin_3, R6.Pin_0
  N17: 7_Segment_4_Digit_Display1.pin_4, R7.Pin_0
  N18: 7_Segment_4_Digit_Display1.pin_5, R8.Pin_0
  N19: 7_Segment_4_Digit_Display1.pin_7, R3.Pin_1
  N20: 7_Segment_4_Digit_Display1.pin_10, R2.Pin_1
  N21: 7_Segment_4_Digit_Display1.pin_11, R1.Pin_1
  N22: スイッチ.Pin_3, スイッチ.Pin_4, R9.Pin_0

custom parts:
  7-SEGMENT-4DIGIT common anode: A 7 Segment 4 Digit common anode display, with decimal points
  KY-012 Active Buzzer Module: Active Piezoelectric Buzzer Module Keyes KY-012, it produces single-tone sound when signal is high.
